# Fritzing sketch receiver_schematic (saved by Fritzing 0.9.3b)

parts:
  Part1 = Arduino Micro (Rev3)
  J1 = Basic Servo
  J2 = Basic Servo
  U1 = LIPO-2000mAh [package=lipo-2000]
  Part2 = NRF24L01+ Breakout Board

nets:
  N1: Part1.MOSI, Part2.MOSI
  GND: Part1.GND, J1.gnd, U1.-, Part2.GND
  N2: Part1.D2/SDA, J2.pulse
  N3: Part1.D3/SCL, J1.pulse
  N4: Part1.D5_PWM, Part2.CE
  N5: Part1.D6_PWM/A7, Part2.CS
  N6: Part1.SCK, Part2.SCK
  N7: Part1.MISO, Part2.MISO
  VCC: Part1.5V, J1.vcc, J2.vcc, U1.+
  3V3: Part1.3V3, Part2.VCC
