# Fritzing sketch transmitter_schematic (saved by Fritzing 0.9.3b)

parts:
  Part1 = Arduino Micro (Rev3)
  U1 = LIPO-2000mAh [package=lipo-2000]
  Part2 = NRF24L01+ Breakout Board
  Part3 = Thumb Joystick

nets:
  N1: Part1.MOSI, Part2.MOSI
  GND: Part1.GND, U1.-, Part3.GND
  N2: Part1.D5_PWM, Part2.CE
  N3: Part1.D6_PWM/A7, Part2.CS
  N4: Part1.D10_PWM/A10, Part3.SEL
  N5: Part1.SCK, Part2.SCK
  N6: Part1.MISO, Part2.MISO
  N7: Part1.A1, Part3.VERT
  N8: Part1.A0, Part3.HORZ
  3V3: Part1.3V3, Part2.VCC
  N9: U1.+, Part3.VCC
